# Fritzing sketch heart_scheme_pcb (saved by Fritzing 0.9.3b)
circuit board: 6cm x 5.48595cm

parts:
  U1 = atmega168 [package=dip]
  OLED_I2C1 = OLED 128x64 I2C Monochrome Display
  SENSOR = Pulse Sensor [package=SIP]
  USB = USB_MICROB_PLUG [package=micro-b-ra-th]

nets:
  VCC: U1.VCC, OLED_I2C1.VDD, SENSOR.Vcc, USB.VCC
  GND: U1.GND, OLED_I2C1.GND, SENSOR.GND, USB.GND
  N1: U1.A3, SENSOR.Signal
  N2: U1.A4, OLED_I2C1.SDA
  N3: U1.A5, OLED_I2C1.SCK

custom parts:
  Pulse Sensor: Pulse Sensor Optical Heart Rate Monitor for Arduino and other microcontrollers
